# Fritzing sketch Koblingskjema (saved by Fritzing 0.9.3b)
breadboards: 1

parts:
  Part1 = Photon
  GY1 = MPU-6050 Board GY-521 [form="♀ (female)" package=THT]
  IC1 = AD8232 HeartRate Monitor [part_number=SEN-12650 chip_label=IC package="DIP (Dual Inline) [THT]"]
  S1 = Pushbutton [package="[SMD]"]
  S2 = Pushbutton [package="[SMD]"]
  R1 = Resistor [tolerance=±5% resistance=10k package=THT]
  R2 = Resistor [tolerance=±5% resistance=10k package=THT]

nets:
  N1: Part1.A3, GY1.pin3
  N2: Part1.A4, IC1.OUTPUT
  N3: Part1.A5, GY1.pin4
  GND: Part1.GND, GY1.pin2, IC1.GND, R1.Pin_0, R2.Pin_0
  VIN: Part1.VIN, GY1.pin1, IC1.3.3v, S1.Pin_3, S1.Pin_4, S2.Pin_3, S2.Pin_4
  N4: Part1.D0, IC1.LO+
  N5: Part1.D1, IC1.LO-
  N6: Part1.D4, S2.Pin_1, S2.Pin_2, R1.Pin_1
  N7: Part1.D5, S1.Pin_1, S1.Pin_2, R2.Pin_1

custom parts:
  MPU-6050 Board GY-521: Acelerometro y Giroscopio MPU-6050 Board GY-521
  AD8232 HeartRate Monitor: A DIP stand-in part for whatever IC you want. With 10 pins on a 600mil dual inline package (DIP) footprint.
